# Fritzing sketch Sketch (saved by Fritzing 0.9.3b)
breadboards: 1

parts:
  part = Rectifier Diode [part_number=1N4001 package="300 mil [THT]"]
  part_2 = Rectifier Diode [part_number=1N4001 package="300 mil [THT]"]
  part_3 = Resistor [tolerance=±5% resistance=10k package=THT]
  U1 = attiny85 [package=dip]
  WeMos_D1_Mini1 = WeMos D1 Mini
  LED = LED - 5mm [color="Red (633nm)" package="5 mm [THT]"]
  part_4 = Resistor [tolerance=±5% resistance=220 package=THT]
  U3 = ESP32-38PinWide [part_number=ESP32-38PinWide]
  5V = DC Power [voltage=5]

nets:
  N1: part.cathode, U1.Pin_5
  N2: part.anode, part_2.anode, part_3.Pin_1, WeMos_D1_Mini1.RX
  N3: part_2.cathode, U3.GPIO1
  N4: part_3.Pin_0, U1.Pin_8, WeMos_D1_Mini1.3V3
  N5: U1.Pin_3, LED.anode
  N6: U1.Pin_4, WeMos_D1_Mini1.G, part_4.Pin_0, U3.GND, 5V.V-
  N7: U1.Pin_6, WeMos_D1_Mini1.TX, U3.GPIO3
  5V: WeMos_D1_Mini1.5V, U3.VIN, 5V.V+
  N8: LED.cathode, part_4.Pin_1

custom parts:
  ESP32-38PinWide: Generic 38-Pin ESP32 with wide format (only access to one side of pins on a breadboard) based on Stephen Lilley's HiLetgo ESP-WROOM-32 ESP32 ESP-32S Development Board.
